// Logisim project 01_logic4.circ as structural Verilog
module P1_logic (
  input  a,
  input  b,
  input  c,
  input  d,
  output out1,
  output out2
);

  logic4 logic4_1 (.a(a), .b(b), .c(c), .d(d), .out1(out1), .out2(out2));

  // Notes on the sheet:
  //   a: initial=0x1
  //   b: initial=0x1
  //   c: initial=0x1
  //   d: initial=0x1
  //   1. Four-input AND and OR
  //   Poke inputs to change values. Enable VHDL simulation in the Simulate menu.
  //   AND = 1 only when a=b=c=d=1.
  //   OR = 1 when at least one input is 1.
endmodule

// VHDL entity logic4, as the project stores it:
library ieee;
use ieee.std_logic_1164.all;

-- Problem 1: four-input AND and OR gates.
entity logic4 is
    port (
        a, b, c, d : in  std_logic;
        out1       : out std_logic;
        out2       : out std_logic
    );
end entity logic4;

architecture rtl of logic4 is
begin
    out1 <= a and b and c and d;
    out2 <= a or b or c or d;
end architecture rtl;
