// Logisim project 02_mux8_1.circ as structural Verilog
module P2_mux (
  input  a,
  input  b,
  input  c,
  input  d,
  input  e,
  input  f,
  input  g,
  input  h,
  input  [2:0] ch,
  output data
);

  mux8_1 mux8_1_1 (.a(a), .b(b), .c(c), .d(d), .e(e), .f(f), .g(g), .h(h), .ch(ch), .data(data));

  // Notes on the sheet:
  //   e: initial=0x1
  //   ch: initial=0x4
  //   2. Eight-to-one multiplexer
  //   Poke inputs to change values. Enable VHDL simulation in the Simulate menu.
  //   ch: 000=a, 001=b, 010=c, 011=d, 100=e, 101=f, 110=g, 111=h.
  //   Initial example: only e=1; ch=100 selects e, so data=1.
endmodule

// VHDL entity mux8_1, as the project stores it:
library ieee;
use ieee.std_logic_1164.all;

-- Problem 2: ch=000 selects a, ..., ch=111 selects h.
entity mux8_1 is
    port (
        a, b, c, d, e, f, g, h : in  std_logic;
        ch                      : in  std_logic_vector(2 downto 0);
        data                    : out std_logic
    );
end entity mux8_1;

architecture rtl of mux8_1 is
begin
    with ch select
        data <= a   when "000",
                b   when "001",
                c   when "010",
                d   when "011",
                e   when "100",
                f   when "101",
                g   when "110",
                h   when "111",
                '0' when others;
end architecture rtl;
