// Logisim project 03_letter_display.circ as structural Verilog
module P3_letters (
  input  en,
  input  [2:0] dat,
  output [7:0] segments_hex
);

  letter_display letter_display_1 (.en(en), .dat(dat), .display(segments_hex));
  _7_Segment_Display #(.active("true"), .decimalPoint("true")) u_7_segment_display_1 (
    .g(segments_hex[1]), .f(segments_hex[2]), .a(segments_hex[7]), .b(segments_hex[6]), .e(segments_hex[3]),
    .d(segments_hex[4]), .c(segments_hex[5]), .dp(segments_hex[0]));

  // Other names for the same wires on the sheet: dp = segments_hex[0]; g = segments_hex[1]; f = segments_hex[2];
  //   e = segments_hex[3]; d = segments_hex[4]; c = segments_hex[5]; b = segments_hex[6]; a = segments_hex[7]

  // Notes on the sheet:
  //   en: initial=0x1
  //   3. Letter decoder and seven-segment display
  //   Poke inputs to change values. Enable VHDL simulation in the Simulate menu.
  //   dat: 0=A, 1=b, 2=C, 3=d, 4=F, 5=G; 6/7=blank.
  //   en=0 blanks the display. Output order: abcdefgdp.
  //   1 = segment ON; dp always OFF.
endmodule

// VHDL entity letter_display, as the project stores it:
library ieee;
use ieee.std_logic_1164.all;

-- Problem 3: display the letters a, b, c, d, f, g.
-- Seven-segment approximations: A, b, C, d, F, G.
-- display(7 downto 0) = a b c d e f g dp; 1 = segment on.
-- dat: 000=A, 001=b, 010=C, 011=d, 100=F, 101=G.
entity letter_display is
    port (
        en      : in  std_logic;
        dat     : in  std_logic_vector(2 downto 0);
        display : out std_logic_vector(7 downto 0)
    );
end entity letter_display;

architecture rtl of letter_display is
begin
    process(en, dat)
    begin
        display <= "00000000";
        if en = '1' then
            case dat is
                when "000" => display <= "11101110"; -- A
                when "001" => display <= "00111110"; -- b
                when "010" => display <= "10011100"; -- C
                when "011" => display <= "01111010"; -- d
                when "100" => display <= "10001110"; -- F
                when "101" => display <= "10111100"; -- G
                when others => display <= "00000000";
            end case;
        end if;
    end process;
end architecture rtl;
