// Logisim project 04_vote25.circ as structural Verilog
module P4_vote25 (
  input  [24:0] vt,
  output result
);

  vote25 vote25_1 (.vt(vt), .result(result));

  // Notes on the sheet:
  //   vt: initial=0x1fff
  //   4. Twenty-five-person majority vote
  //   Poke inputs to change values. Enable VHDL simulation in the Simulate menu.
  //   vt is hexadecimal. 0000FFF = 12 yes votes; 0001FFF = 13 yes votes.
  //   A strict majority requires at least 13 votes.
endmodule

// VHDL entity vote25, as the project stores it:
library ieee;
use ieee.std_logic_1164.all;

-- Problem 4: a strict majority of 25 voters requires at least 13 votes.
entity vote25 is
    port (
        vt     : in  std_logic_vector(25 downto 1);
        result : out std_logic
    );
end entity vote25;

architecture rtl of vote25 is
begin
    process(vt)
        variable sum : integer range 0 to 25;
    begin
        sum := 0;
        for i in vt'range loop
            if vt(i) = '1' then
                sum := sum + 1;
            end if;
        end loop;

        if sum >= 13 then
            result <= '1';
        else
            result <= '0';
        end if;
    end process;
end architecture rtl;
