// Logisim project 05_count13_display.circ as structural Verilog
module P5_count13 (
  input  [12:0] vt,
  input  en,
  output [7:0] segments_hex
);

  count13_display count13_display_1 (.vt(vt), .en(en), .display(segments_hex));
  _7_Segment_Display #(.active("true"), .decimalPoint("true")) u_7_segment_display_1 (
    .g(segments_hex[1]), .f(segments_hex[2]), .a(segments_hex[7]), .b(segments_hex[6]), .e(segments_hex[3]),
    .d(segments_hex[4]), .c(segments_hex[5]), .dp(segments_hex[0]));

  // Other names for the same wires on the sheet: dp = segments_hex[0]; g = segments_hex[1]; f = segments_hex[2];
  //   e = segments_hex[3]; d = segments_hex[4]; c = segments_hex[5]; b = segments_hex[6]; a = segments_hex[7]

  // Notes on the sheet:
  //   vt: initial=0x1fff
  //   en: initial=0x1
  //   5. Count ones in thirteen bits and display the count
  //   Poke inputs to change values. Enable VHDL simulation in the Simulate menu.
  //   vt is hexadecimal. 0005 -> 2; 03FF -> A; 1FFF -> d.
  //   Thirteen bits contain at most thirteen ones. E/F cannot be reached.
  //   en=0 blanks all segments, including the decimal point.
  //   1 = segment ON; dp always OFF.
endmodule

// VHDL entity count13_display, as the project stores it:
library ieee;
use ieee.std_logic_1164.all;

-- Problem 5: count the ones in vt and display the hexadecimal count.
-- display(7 downto 0) = a b c d e f g dp; 1 = segment on.
-- A 13-bit input can produce only 0..13; E/F entries are unreachable.
entity count13_display is
    port (
        vt      : in  std_logic_vector(13 downto 1);
        en      : in  std_logic;
        display : out std_logic_vector(7 downto 0)
    );
end entity count13_display;

architecture rtl of count13_display is
begin
    process(vt, en)
        variable sum : integer range 0 to 15;
    begin
        sum := 0;
        for i in vt'range loop
            if vt(i) = '1' then
                sum := sum + 1;
            end if;
        end loop;

        display <= "00000000";
        if en = '1' then
            case sum is
                when  0 => display <= "11111100";
                when  1 => display <= "01100000";
                when  2 => display <= "11011010";
                when  3 => display <= "11110010";
                when  4 => display <= "01100110";
                when  5 => display <= "10110110";
                when  6 => display <= "10111110";
                when  7 => display <= "11100000";
                when  8 => display <= "11111110";
                when  9 => display <= "11110110";
                when 10 => display <= "11101110"; -- A
                when 11 => display <= "00111110"; -- b
                when 12 => display <= "10011100"; -- C
                when 13 => display <= "01111010"; -- d
                when 14 => display <= "10011110"; -- E
                when 15 => display <= "10001110"; -- F
                when others => display <= "00000000";
            end case;
        end if;
    end process;
end architecture rtl;
