// Logisim project VHDL1_all.circ as structural Verilog
module P1_logic (
  input  a,
  input  b,
  input  c,
  input  d,
  output out1,
  output out2
);

  logic4 logic4_1 (.a(a), .b(b), .c(c), .d(d), .out1(out1), .out2(out2));

  // Notes on the sheet:
  //   a: initial=0x1
  //   b: initial=0x1
  //   c: initial=0x1
  //   d: initial=0x1
  //   1. Four-input AND and OR
  //   Poke inputs to change values. Enable VHDL simulation in the Simulate menu.
  //   AND = 1 only when a=b=c=d=1.
  //   OR = 1 when at least one input is 1.
endmodule

module P2_mux (
  input  a,
  input  b,
  input  c,
  input  d,
  input  e,
  input  f,
  input  g,
  input  h,
  input  [2:0] ch,
  output data
);

  mux8_1 mux8_1_1 (.a(a), .b(b), .c(c), .d(d), .e(e), .f(f), .g(g), .h(h), .ch(ch), .data(data));

  // Notes on the sheet:
  //   e: initial=0x1
  //   ch: initial=0x4
  //   2. Eight-to-one multiplexer
  //   Poke inputs to change values. Enable VHDL simulation in the Simulate menu.
  //   ch: 000=a, 001=b, 010=c, 011=d, 100=e, 101=f, 110=g, 111=h.
  //   Initial example: only e=1; ch=100 selects e, so data=1.
endmodule

module P3_letters (
  input  en,
  input  [2:0] dat,
  output [7:0] segments_hex
);

  letter_display letter_display_1 (.en(en), .dat(dat), .display(segments_hex));
  _7_Segment_Display #(.active("true"), .decimalPoint("true")) u_7_segment_display_1 (
    .g(segments_hex[1]), .f(segments_hex[2]), .a(segments_hex[7]), .b(segments_hex[6]), .e(segments_hex[3]),
    .d(segments_hex[4]), .c(segments_hex[5]), .dp(segments_hex[0]));

  // Other names for the same wires on the sheet: dp = segments_hex[0]; g = segments_hex[1]; f = segments_hex[2];
  //   e = segments_hex[3]; d = segments_hex[4]; c = segments_hex[5]; b = segments_hex[6]; a = segments_hex[7]

  // Notes on the sheet:
  //   en: initial=0x1
  //   3. Letter decoder and seven-segment display
  //   Poke inputs to change values. Enable VHDL simulation in the Simulate menu.
  //   dat: 0=A, 1=b, 2=C, 3=d, 4=F, 5=G; 6/7=blank.
  //   en=0 blanks the display. Output order: abcdefgdp.
  //   1 = segment ON; dp always OFF.
endmodule

module P4_vote25 (
  input  [24:0] vt,
  output result
);

  vote25 vote25_1 (.vt(vt), .result(result));

  // Notes on the sheet:
  //   vt: initial=0x1fff
  //   4. Twenty-five-person majority vote
  //   Poke inputs to change values. Enable VHDL simulation in the Simulate menu.
  //   vt is hexadecimal. 0000FFF = 12 yes votes; 0001FFF = 13 yes votes.
  //   A strict majority requires at least 13 votes.
endmodule

module P5_count13 (
  input  [12:0] vt,
  input  en,
  output [7:0] segments_hex
);

  count13_display count13_display_1 (.vt(vt), .en(en), .display(segments_hex));
  _7_Segment_Display #(.active("true"), .decimalPoint("true")) u_7_segment_display_1 (
    .g(segments_hex[1]), .f(segments_hex[2]), .a(segments_hex[7]), .b(segments_hex[6]), .e(segments_hex[3]),
    .d(segments_hex[4]), .c(segments_hex[5]), .dp(segments_hex[0]));

  // Other names for the same wires on the sheet: dp = segments_hex[0]; g = segments_hex[1]; f = segments_hex[2];
  //   e = segments_hex[3]; d = segments_hex[4]; c = segments_hex[5]; b = segments_hex[6]; a = segments_hex[7]

  // Notes on the sheet:
  //   vt: initial=0x1fff
  //   en: initial=0x1
  //   5. Count ones in thirteen bits and display the count
  //   Poke inputs to change values. Enable VHDL simulation in the Simulate menu.
  //   vt is hexadecimal. 0005 -> 2; 03FF -> A; 1FFF -> d.
  //   Thirteen bits contain at most thirteen ones. E/F cannot be reached.
  //   en=0 blanks all segments, including the decimal point.
  //   1 = segment ON; dp always OFF.
endmodule

// VHDL entity logic4, as the project stores it:
library ieee;
use ieee.std_logic_1164.all;

-- Problem 1: four-input AND and OR gates.
entity logic4 is
    port (
        a, b, c, d : in  std_logic;
        out1       : out std_logic;
        out2       : out std_logic
    );
end entity logic4;

architecture rtl of logic4 is
begin
    out1 <= a and b and c and d;
    out2 <= a or b or c or d;
end architecture rtl;

// VHDL entity mux8_1, as the project stores it:
library ieee;
use ieee.std_logic_1164.all;

-- Problem 2: ch=000 selects a, ..., ch=111 selects h.
entity mux8_1 is
    port (
        a, b, c, d, e, f, g, h : in  std_logic;
        ch                      : in  std_logic_vector(2 downto 0);
        data                    : out std_logic
    );
end entity mux8_1;

architecture rtl of mux8_1 is
begin
    with ch select
        data <= a   when "000",
                b   when "001",
                c   when "010",
                d   when "011",
                e   when "100",
                f   when "101",
                g   when "110",
                h   when "111",
                '0' when others;
end architecture rtl;

// VHDL entity letter_display, as the project stores it:
library ieee;
use ieee.std_logic_1164.all;

-- Problem 3: display the letters a, b, c, d, f, g.
-- Seven-segment approximations: A, b, C, d, F, G.
-- display(7 downto 0) = a b c d e f g dp; 1 = segment on.
-- dat: 000=A, 001=b, 010=C, 011=d, 100=F, 101=G.
entity letter_display is
    port (
        en      : in  std_logic;
        dat     : in  std_logic_vector(2 downto 0);
        display : out std_logic_vector(7 downto 0)
    );
end entity letter_display;

architecture rtl of letter_display is
begin
    process(en, dat)
    begin
        display <= "00000000";
        if en = '1' then
            case dat is
                when "000" => display <= "11101110"; -- A
                when "001" => display <= "00111110"; -- b
                when "010" => display <= "10011100"; -- C
                when "011" => display <= "01111010"; -- d
                when "100" => display <= "10001110"; -- F
                when "101" => display <= "10111100"; -- G
                when others => display <= "00000000";
            end case;
        end if;
    end process;
end architecture rtl;

// VHDL entity vote25, as the project stores it:
library ieee;
use ieee.std_logic_1164.all;

-- Problem 4: a strict majority of 25 voters requires at least 13 votes.
entity vote25 is
    port (
        vt     : in  std_logic_vector(25 downto 1);
        result : out std_logic
    );
end entity vote25;

architecture rtl of vote25 is
begin
    process(vt)
        variable sum : integer range 0 to 25;
    begin
        sum := 0;
        for i in vt'range loop
            if vt(i) = '1' then
                sum := sum + 1;
            end if;
        end loop;

        if sum >= 13 then
            result <= '1';
        else
            result <= '0';
        end if;
    end process;
end architecture rtl;

// VHDL entity count13_display, as the project stores it:
library ieee;
use ieee.std_logic_1164.all;

-- Problem 5: count the ones in vt and display the hexadecimal count.
-- display(7 downto 0) = a b c d e f g dp; 1 = segment on.
-- A 13-bit input can produce only 0..13; E/F entries are unreachable.
entity count13_display is
    port (
        vt      : in  std_logic_vector(13 downto 1);
        en      : in  std_logic;
        display : out std_logic_vector(7 downto 0)
    );
end entity count13_display;

architecture rtl of count13_display is
begin
    process(vt, en)
        variable sum : integer range 0 to 15;
    begin
        sum := 0;
        for i in vt'range loop
            if vt(i) = '1' then
                sum := sum + 1;
            end if;
        end loop;

        display <= "00000000";
        if en = '1' then
            case sum is
                when  0 => display <= "11111100";
                when  1 => display <= "01100000";
                when  2 => display <= "11011010";
                when  3 => display <= "11110010";
                when  4 => display <= "01100110";
                when  5 => display <= "10110110";
                when  6 => display <= "10111110";
                when  7 => display <= "11100000";
                when  8 => display <= "11111110";
                when  9 => display <= "11110110";
                when 10 => display <= "11101110"; -- A
                when 11 => display <= "00111110"; -- b
                when 12 => display <= "10011100"; -- C
                when 13 => display <= "01111010"; -- d
                when 14 => display <= "10011110"; -- E
                when 15 => display <= "10001110"; -- F
                when others => display <= "00000000";
            end case;
        end if;
    end process;
end architecture rtl;
