// Logisim project not_gate.circ as structural Verilog
module main (
  input  in_1,
  output out_2
);

  not_gate not_gate_1 (.a(in_1), .y(out_2));
endmodule

// VHDL entity not_gate, as the project stores it:
LIBRARY ieee;
USE ieee.std_logic_1164.all;

ENTITY not_gate IS
  PORT (
    a : IN  std_logic; -- 입력
    y : OUT std_logic  -- 출력
  );
END not_gate;

ARCHITECTURE TypeArchitecture OF not_gate IS
BEGIN
    y <= NOT a; -- NOT 동작
END TypeArchitecture;
